// Logisim project FullandHalfadders.circ as structural Verilog: 3 circuits, main circuit main
module main (
  input  in_1,
  input  in_2,
  input  in_3,
  input  in_4,
  output out_5,
  output out_6,
  output out_7,
  output out_8
);

  halfadder halfadder_1 ();  // open: A, B, out_3, out_4
  halfadder halfadder_2 (.A(in_3), .B(in_4), .out_3(out_7), .out_4(out_8));
  Fulladder fulladder_1 ();  // open: CarryIn, B, A, Sum, Carryout
  xor xor_1 (out_5, in_1, in_2);
  // AND_Gate and_1 has open pins: in1=in_2, out=open
endmodule

module halfadder (
  input  A,
  input  B,
  output out_3,
  output out_4
);

  xor xor_1 (out_3, A, B);
  and and_1 (out_4, A, B);
endmodule

module Fulladder (
  input  CarryIn,
  input  B,
  input  A,
  output Sum,
  output Carryout
);

  wire and_1_out, and_2_out, xor_1_out;

  xor xor_1 (xor_1_out, B, A);
  and and_1 (and_1_out, B, A);
  xor xor_2 (Sum, CarryIn, xor_1_out);
  and and_2 (and_2_out, CarryIn, xor_1_out);
  or or_1 (Carryout, and_2_out, and_1_out);
endmodule
